# Fritzing sketch SmartIrrigationSystem (saved by Fritzing 0.9.10b)
breadboards: 1

parts:
  U1 = ESP8266 WiFi Module [part_number=ESP8266]
  Part1 = Soil Moisture Sensor
  KY-1 = Keyes Relay [package=THT]
  부품3 = Arduino Uno (Rev3)
  M1 = DC Motor [voltage_(max)=6V voltage_(min)=3V]
  VCC1 = Battery block 9V

nets:
  N1: U1.RXD, 부품3.D2
  VCC: U1.VCC, U1.CH_PD, 부품3.3V3
  GND: U1.GND, Part1.GND, KY-1.ground, 부품3.GND
  N2: U1.TXD, 부품3.D3_PWM
  N3: Part1.SIG, 부품3.A0
  VCC_2: Part1.VCC, KY-1.power, 부품3.5V
  N4: KY-1.signal, 부품3.D13/SCK
  N5: KY-1.C, VCC1.+
  N6: KY-1.NO, M1.pin_1

notes:
  5v power
  3v power
  soil moisture sensor
  ESP8266
  Rlay
  Motor
  Arduino Output
  Arduino Input
  AC ground
  AC  power
  Ground
  Wires key
  Power

custom parts:
  ESP8266 WiFi Module: Generic WiFi Module based on the ESP8266 with onboard PCB antenna and UART communications
  Keyes Relay: The Keyes 5V relay module is suitable for SCM development, home appliance control. It uses a 5V~12V TIL control signal which can control DC / AC signal.

// code stored in the sketch: SmartIrrigationSystem.ino
#define RELAY_PIN 2 // Arduino pin that connects to relay
#define MOISTURE_PIN A0 // Arduino pin that connects to AOUT pin of moisture sensor

#define THRESHOLD 100 // CHANGE YOUR THRESHOLD HERE

void setup() {
 Serial.begin(9600);
 pinMode(RELAY_PIN, OUTPUT);
}

void loop() {
 int value = analogRead(MOISTURE_PIN); // read the analog value from sensor

 if (value < THRESHOLD) {
 Serial.print("The soil is DRY => turn pump ON");
 digitalWrite(RELAY_PIN, HIGH);
 } else {
 Serial.print("The soil is WET => turn pump OFF");
 digitalWrite(RELAY_PIN, LOW);
 }

 Serial.print(" (");
 Serial.print(value);
 Serial.println(")");

 delay(500);
}
